// Logisim project arquitetura.circ as structural Verilog: 1 circuit, main circuit main
module main (
  output [31:0] out_1
);

  wire and_1_out, dipswitch_1_p1, main_2_alusrc, main_2_branch, main_2_jalornot, main_2_memtoreg,
       main_2_regwrite, main_5_zero, main_6_uc_ula, MemWrite, or_1_out;
  wire [1:0] main_2_alucontrol, main_2_immsrc;
  wire [23:0] main_1_out_2, main_7_out_2;
  wire [31:0] adder_1_out, adder_2_out, main_3_rs1_2, main_3_rs2_2, main_4_out_3, main_5_aluoutput,
       \Memória_de_Dados_data , multiplexer_1_out, multiplexer_2_out, multiplexer_3_out, multiplexer_4_out,
       PC_q;

  Multiplexer #(.width(32), .enable("false")) multiplexer_1 (
    .in0(adder_1_out), .in1(adder_2_out), .out(multiplexer_1_out), .sel(or_1_out));
  // DipSwitch #(.NSwitches(1)) dipswitch_1: pin names not known; wires that end beside it: dipswitch_1_p1
  Register #(.width(32), .trigger("falling"), .Select("low")) PC (
    .D(multiplexer_1_out), .Q(PC_q), .clk(dipswitch_1_p1));  // open: en, clr
  Adder #(.width(32)) adder_1 (.a(PC_q), .b(32'h4), .out(adder_1_out));  // open: cin, cout
  conversor_32_24_main main_1 (.Entrada(PC_q), .out_2(main_1_out_2));
  RAM #(.addrWidth(24), .dataWidth(32), .bus("asynch"), .Select("low")) \Memória_de_Instrução  (
    .addr(main_1_out_2), .data(out_1), .ld(1'b1));  // open: sel, clr
  uc_main main_2 (
    .ImmSrc(main_2_immsrc), .ALUSrc(main_2_alusrc), .ALUControl(main_2_alucontrol), .MemWrite(MemWrite),
    .MemToReg(main_2_memtoreg), .JalOrNot(main_2_jalornot), .RegWrite(main_2_regwrite),
    .Branch(main_2_branch), .Opcode(out_1[6:0]));
  bco_reg_main main_3 (
    .Clock(dipswitch_1_p1), .WriteData(multiplexer_2_out), .rd(out_1[11:7]), .rs1(out_1[24:20]),
    .rs2(out_1[19:15]), .RegWrite(main_2_regwrite), .rs2_2(main_3_rs2_2), .rs1_2(main_3_rs1_2));
  Multiplexer #(.width(32), .enable("false")) multiplexer_2 (
    .in0(multiplexer_4_out), .in1(adder_1_out), .out(multiplexer_2_out), .sel(main_2_jalornot));
  imm_gen_main main_4 (.out_3(main_4_out_3), .in_2(out_1), .ImmSrc(main_2_immsrc));
  or or_1 (or_1_out, main_2_jalornot, and_1_out);
  and and_1 (and_1_out, main_2_branch, main_5_zero);
  ula_main main_5 (
    .ALUOutput(main_5_aluoutput), .B(multiplexer_3_out), .A(main_3_rs1_2), .ALUControl(main_6_uc_ula),
    .Zero(main_5_zero));
  Multiplexer #(.width(32), .enable("false")) multiplexer_3 (
    .in0(main_3_rs2_2), .in1(main_4_out_3), .out(multiplexer_3_out), .sel(main_2_alusrc));
  uc_ula_main main_6 (.ALUControl(main_2_alucontrol), .f3(out_1[14:12]), .f7(out_1[31:25]), .UC_ULA(main_6_uc_ula));
  Adder #(.width(32)) adder_2 (.a(main_4_out_3), .b(PC_q), .out(adder_2_out));  // open: cin, cout
  conversor_32_24_main main_7 (.Entrada(main_5_aluoutput), .out_2(main_7_out_2));
  RAM #(.addrWidth(24), .dataWidth(32), .bus("separate"), .simpleMode("false"), .Select("low")) \Memória_de_Dados  (
    .addr(main_7_out_2), .din(main_3_rs2_2), .data(\Memória_de_Dados_data ), .str(MemWrite),
    .clk(dipswitch_1_p1));  // open: sel, ld, clr
  Multiplexer #(.width(32), .enable("false")) multiplexer_4 (
    .in0(main_5_aluoutput), .in1(\Memória_de_Dados_data ), .out(multiplexer_4_out), .sel(main_2_memtoreg));

  // Notes on the sheet:
  //   para manter a realidade
  //   Cada endereço da RAM armazena 4 bytes, logo para avançar,
  //   em teoria, deveria somar 1 para PC, mas vamos manter PC + 4
endmodule
