// Logisim project banco_de_resgitradores.circ as structural Verilog: 1 circuit, main circuit main
module main (
  input  [4:0] rs2,
  input  [4:0] rs1,
  input  RegWrite,
  input  [4:0] rd,
  input  [31:0] WriteData,
  input  Clock,
  output [31:0] rs1_2,
  output [31:0] rs2_2
);

  wire and_1_out, and_2_out, and_3_out, and_4_out, and_5_out, and_6_out, and_7_out, and_8_out, and_9_out,
       and_10_out, and_11_out, and_12_out, and_13_out, and_14_out, and_15_out, and_16_out, and_17_out,
       and_18_out, and_19_out, and_20_out, and_21_out, and_22_out, and_23_out, and_24_out, and_25_out,
       and_26_out, and_27_out, and_28_out, and_29_out, and_30_out, and_31_out, and_32_out,
       demultiplexer_1_out0, demultiplexer_1_out1, demultiplexer_1_out2, demultiplexer_1_out3,
       demultiplexer_1_out4, demultiplexer_1_out5, demultiplexer_1_out6, demultiplexer_1_out7,
       demultiplexer_2_out0, demultiplexer_2_out1, demultiplexer_2_out2, demultiplexer_2_out3;
  wire [31:0] multiplexer_1_out, multiplexer_2_out, multiplexer_3_out, multiplexer_4_out, multiplexer_5_out,
       multiplexer_6_out, multiplexer_7_out, multiplexer_8_out, multiplexer_9_out, multiplexer_10_out,
       multiplexer_11_out, multiplexer_12_out, multiplexer_13_out, multiplexer_14_out, multiplexer_15_out,
       multiplexer_16_out, register_1_q, register_2_q, register_3_q, register_4_q, register_5_q,
       register_6_q, register_7_q, register_8_q, register_9_q, register_10_q, register_11_q, register_12_q,
       register_13_q, register_14_q, register_15_q, register_16_q, register_17_q, register_18_q,
       register_19_q, register_20_q, register_21_q, register_22_q, register_23_q, register_24_q,
       register_25_q, register_26_q, register_27_q, register_28_q, register_29_q, register_30_q,
       register_31_q, register_32_q;

  Demultiplexer #(.select(3), .enable("false")) demultiplexer_1 (
    .out0(demultiplexer_1_out0), .out1(demultiplexer_1_out1), .out2(demultiplexer_1_out2),
    .out3(demultiplexer_1_out3), .out4(demultiplexer_1_out4), .out5(demultiplexer_1_out5),
    .out6(demultiplexer_1_out6), .out7(demultiplexer_1_out7), .in(RegWrite), .sel(rd[4:2]));
  and and_1 (and_1_out, demultiplexer_2_out0, demultiplexer_1_out0);
  and and_2 (and_2_out, demultiplexer_2_out0, demultiplexer_1_out1);
  and and_3 (and_3_out, demultiplexer_2_out0, demultiplexer_1_out2);
  and and_4 (and_4_out, demultiplexer_2_out0, demultiplexer_1_out3);
  and and_5 (and_5_out, demultiplexer_2_out0, demultiplexer_1_out4);
  and and_6 (and_6_out, demultiplexer_2_out0, demultiplexer_1_out5);
  and and_7 (and_7_out, demultiplexer_2_out0, demultiplexer_1_out6);
  and and_8 (and_8_out, demultiplexer_2_out0, demultiplexer_1_out7);
  Demultiplexer #(.select(2), .enable("false")) demultiplexer_2 (
    .out0(demultiplexer_2_out0), .out1(demultiplexer_2_out1), .out2(demultiplexer_2_out2),
    .out3(demultiplexer_2_out3), .in(RegWrite), .sel(rd[1:0]));
  Register #(.width(32), .Select("low")) register_1 (
    .D({32{1'b0}}), .en(and_1_out), .Q(register_1_q), .clk(Clock));  // open: clr
  Register #(.width(32), .Select("low")) register_2 (
    .D(WriteData), .en(and_2_out), .Q(register_2_q), .clk(Clock));  // open: clr
  Register #(.width(32), .Select("low")) register_3 (
    .D(WriteData), .en(and_3_out), .Q(register_3_q), .clk(Clock));  // open: clr
  Register #(.width(32), .Select("low")) register_4 (
    .D(WriteData), .en(and_4_out), .Q(register_4_q), .clk(Clock));  // open: clr
  Register #(.width(32), .Select("low")) register_5 (
    .D(WriteData), .en(and_5_out), .Q(register_5_q), .clk(Clock));  // open: clr
  Register #(.width(32), .Select("low")) register_6 (
    .D(WriteData), .en(and_6_out), .Q(register_6_q), .clk(Clock));  // open: clr
  Register #(.width(32), .Select("low")) register_7 (
    .D(WriteData), .en(and_7_out), .Q(register_7_q), .clk(Clock));  // open: clr
  Register #(.width(32), .Select("low")) register_8 (
    .D(WriteData), .en(and_8_out), .Q(register_8_q), .clk(Clock));  // open: clr
  Register #(.width(32), .Select("low")) register_9 (
    .D(WriteData), .en(and_9_out), .Q(register_9_q), .clk(Clock));  // open: clr
  and and_9 (and_9_out, demultiplexer_2_out1, demultiplexer_1_out0);
  Register #(.width(32), .Select("low")) register_10 (
    .D(WriteData), .en(and_10_out), .Q(register_10_q), .clk(Clock));  // open: clr
  and and_10 (and_10_out, demultiplexer_2_out1, demultiplexer_1_out1);
  Register #(.width(32), .Select("low")) register_11 (
    .D(WriteData), .en(and_11_out), .Q(register_11_q), .clk(Clock));  // open: clr
  and and_11 (and_11_out, demultiplexer_2_out1, demultiplexer_1_out2);
  Register #(.width(32), .Select("low")) register_12 (
    .D(WriteData), .en(and_12_out), .Q(register_12_q), .clk(Clock));  // open: clr
  and and_12 (and_12_out, demultiplexer_2_out1, demultiplexer_1_out3);
  Register #(.width(32), .Select("low")) register_13 (
    .D(WriteData), .en(and_13_out), .Q(register_13_q), .clk(Clock));  // open: clr
  and and_13 (and_13_out, demultiplexer_2_out1, demultiplexer_1_out4);
  Register #(.width(32), .Select("low")) register_14 (
    .D(WriteData), .en(and_14_out), .Q(register_14_q), .clk(Clock));  // open: clr
  and and_14 (and_14_out, demultiplexer_2_out1, demultiplexer_1_out5);
  Register #(.width(32), .Select("low")) register_15 (
    .D(WriteData), .en(and_15_out), .Q(register_15_q), .clk(Clock));  // open: clr
  and and_15 (and_15_out, demultiplexer_2_out1, demultiplexer_1_out6);
  Register #(.width(32), .Select("low")) register_16 (
    .D(WriteData), .en(and_16_out), .Q(register_16_q), .clk(Clock));  // open: clr
  and and_16 (and_16_out, demultiplexer_2_out1, demultiplexer_1_out7);
  and and_17 (and_17_out, demultiplexer_2_out2, demultiplexer_1_out0);
  and and_18 (and_18_out, demultiplexer_2_out2, demultiplexer_1_out1);
  and and_19 (and_19_out, demultiplexer_2_out2, demultiplexer_1_out2);
  and and_20 (and_20_out, demultiplexer_2_out2, demultiplexer_1_out3);
  and and_21 (and_21_out, demultiplexer_2_out2, demultiplexer_1_out4);
  and and_22 (and_22_out, demultiplexer_2_out2, demultiplexer_1_out5);
  and and_23 (and_23_out, demultiplexer_2_out2, demultiplexer_1_out6);
  and and_24 (and_24_out, demultiplexer_2_out2, demultiplexer_1_out7);
  Register #(.width(32), .Select("low")) register_17 (
    .D(WriteData), .en(and_17_out), .Q(register_17_q), .clk(Clock));  // open: clr
  Register #(.width(32), .Select("low")) register_18 (
    .D(WriteData), .en(and_18_out), .Q(register_18_q), .clk(Clock));  // open: clr
  Register #(.width(32), .Select("low")) register_19 (
    .D(WriteData), .en(and_19_out), .Q(register_19_q), .clk(Clock));  // open: clr
  Register #(.width(32), .Select("low")) register_20 (
    .D(WriteData), .en(and_20_out), .Q(register_20_q), .clk(Clock));  // open: clr
  Register #(.width(32), .Select("low")) register_21 (
    .D(WriteData), .en(and_21_out), .Q(register_21_q), .clk(Clock));  // open: clr
  Register #(.width(32), .Select("low")) register_22 (
    .D(WriteData), .en(and_22_out), .Q(register_22_q), .clk(Clock));  // open: clr
  Register #(.width(32), .Select("low")) register_23 (
    .D(WriteData), .en(and_23_out), .Q(register_23_q), .clk(Clock));  // open: clr
  Register #(.width(32), .Select("low")) register_24 (
    .D(WriteData), .en(and_24_out), .Q(register_24_q), .clk(Clock));  // open: clr
  Register #(.width(32), .Select("low")) register_25 (
    .D(WriteData), .en(and_25_out), .Q(register_25_q), .clk(Clock));  // open: clr
  and and_25 (and_25_out, demultiplexer_2_out3, demultiplexer_1_out0);
  Register #(.width(32), .Select("low")) register_26 (
    .D(WriteData), .en(and_26_out), .Q(register_26_q), .clk(Clock));  // open: clr
  and and_26 (and_26_out, demultiplexer_2_out3, demultiplexer_1_out1);
  Register #(.width(32), .Select("low")) register_27 (
    .D(WriteData), .en(and_27_out), .Q(register_27_q), .clk(Clock));  // open: clr
  and and_27 (and_27_out, demultiplexer_2_out3, demultiplexer_1_out2);
  Register #(.width(32), .Select("low")) register_28 (
    .D(WriteData), .en(and_28_out), .Q(register_28_q), .clk(Clock));  // open: clr
  and and_28 (and_28_out, demultiplexer_2_out3, demultiplexer_1_out3);
  Register #(.width(32), .Select("low")) register_29 (
    .D(WriteData), .en(and_29_out), .Q(register_29_q), .clk(Clock));  // open: clr
  and and_29 (and_29_out, demultiplexer_2_out3, demultiplexer_1_out4);
  Register #(.width(32), .Select("low")) register_30 (
    .D(WriteData), .en(and_30_out), .Q(register_30_q), .clk(Clock));  // open: clr
  and and_30 (and_30_out, demultiplexer_2_out3, demultiplexer_1_out5);
  Register #(.width(32), .Select("low")) register_31 (
    .D(WriteData), .en(and_31_out), .Q(register_31_q), .clk(Clock));  // open: clr
  and and_31 (and_31_out, demultiplexer_2_out3, demultiplexer_1_out6);
  Register #(.width(32), .Select("low")) register_32 (
    .D(WriteData), .en(and_32_out), .Q(register_32_q), .clk(Clock));  // open: clr
  and and_32 (and_32_out, demultiplexer_2_out3, demultiplexer_1_out7);
  Multiplexer #(.select(2), .width(32), .enable("false")) multiplexer_1 (
    .in0(register_1_q), .in1(register_9_q), .in2(register_17_q), .in3(register_25_q),
    .out(multiplexer_1_out), .sel(rs2[1:0]));
  Multiplexer #(.select(2), .width(32), .enable("false")) multiplexer_2 (
    .in0(register_1_q), .in1(register_9_q), .in2(register_17_q), .in3(register_25_q),
    .out(multiplexer_2_out), .sel(rs1[1:0]));
  Multiplexer #(.select(2), .width(32), .enable("false")) multiplexer_3 (
    .in0(register_2_q), .in1(register_10_q), .in2(register_18_q), .in3(register_26_q),
    .out(multiplexer_3_out), .sel(rs2[1:0]));
  Multiplexer #(.select(2), .width(32), .enable("false")) multiplexer_4 (
    .in0(register_2_q), .in1(register_10_q), .in2(register_18_q), .in3(register_26_q),
    .out(multiplexer_4_out), .sel(rs1[1:0]));
  Multiplexer #(.select(2), .width(32), .enable("false")) multiplexer_5 (
    .in0(register_3_q), .in1(register_11_q), .in2(register_19_q), .in3(register_27_q),
    .out(multiplexer_5_out), .sel(rs2[1:0]));
  Multiplexer #(.select(2), .width(32), .enable("false")) multiplexer_6 (
    .in0(register_3_q), .in1(register_11_q), .in2(register_19_q), .in3(register_27_q),
    .out(multiplexer_6_out), .sel(rs1[1:0]));
  Multiplexer #(.select(2), .width(32), .enable("false")) multiplexer_7 (
    .in0(register_4_q), .in1(register_12_q), .in2(register_20_q), .in3(register_28_q),
    .out(multiplexer_7_out), .sel(rs2[1:0]));
  Multiplexer #(.select(2), .width(32), .enable("false")) multiplexer_8 (
    .in0(register_4_q), .in1(register_12_q), .in2(register_20_q), .in3(register_28_q),
    .out(multiplexer_8_out), .sel(rs1[1:0]));
  Multiplexer #(.select(2), .width(32), .enable("false")) multiplexer_9 (
    .in0(register_5_q), .in1(register_13_q), .in2(register_21_q), .in3(register_29_q),
    .out(multiplexer_9_out), .sel(rs2[1:0]));
  Multiplexer #(.select(2), .width(32), .enable("false")) multiplexer_10 (
    .in0(register_5_q), .in1(register_13_q), .in2(register_21_q), .in3(register_29_q),
    .out(multiplexer_10_out), .sel(rs1[1:0]));
  Multiplexer #(.select(2), .width(32), .enable("false")) multiplexer_11 (
    .in0(register_6_q), .in1(register_14_q), .in2(register_22_q), .in3(register_30_q),
    .out(multiplexer_11_out), .sel(rs2[1:0]));
  Multiplexer #(.select(2), .width(32), .enable("false")) multiplexer_12 (
    .in0(register_6_q), .in1(register_14_q), .in2(register_22_q), .in3(register_30_q),
    .out(multiplexer_12_out), .sel(rs1[1:0]));
  Multiplexer #(.select(2), .width(32), .enable("false")) multiplexer_13 (
    .in0(register_7_q), .in1(register_15_q), .in2(register_23_q), .in3(register_31_q),
    .out(multiplexer_13_out), .sel(rs2[1:0]));
  Multiplexer #(.select(2), .width(32), .enable("false")) multiplexer_14 (
    .in0(register_7_q), .in1(register_15_q), .in2(register_23_q), .in3(register_31_q),
    .out(multiplexer_14_out), .sel(rs1[1:0]));
  Multiplexer #(.select(2), .width(32), .enable("false")) multiplexer_15 (
    .in0(register_8_q), .in1(register_16_q), .in2(register_24_q), .in3(register_32_q),
    .out(multiplexer_15_out), .sel(rs2[1:0]));
  Multiplexer #(.select(2), .width(32), .enable("false")) multiplexer_16 (
    .in0(register_8_q), .in1(register_16_q), .in2(register_24_q), .in3(register_32_q),
    .out(multiplexer_16_out), .sel(rs1[1:0]));
  Multiplexer #(.select(3), .width(32), .enable("false")) multiplexer_17 (
    .in0(multiplexer_1_out), .in1(multiplexer_3_out), .in2(multiplexer_5_out), .in3(multiplexer_7_out),
    .in4(multiplexer_9_out), .in5(multiplexer_11_out), .in6(multiplexer_13_out), .in7(multiplexer_15_out),
    .out(rs2_2), .sel(rs2[4:2]));
  Multiplexer #(.select(3), .width(32), .enable("false")) multiplexer_18 (
    .in0(multiplexer_2_out), .in1(multiplexer_4_out), .in2(multiplexer_6_out), .in3(multiplexer_8_out),
    .in4(multiplexer_10_out), .in5(multiplexer_12_out), .in6(multiplexer_14_out), .in7(multiplexer_16_out),
    .out(rs1_2), .sel(rs1[4:2]));
endmodule
