// Logisim project conversor_32_para_24.circ as structural Verilog: 1 circuit, main circuit main
module main (
  input  [31:0] Entrada,
  output [23:0] out_2
);


  assign out_2 = Entrada[23:0];
endmodule
