// Logisim project detector_tipo_instrucao.circ as structural Verilog: 1 circuit, main circuit main
module main (
  input  [6:0] Opcode,
  output Tipor_R,
  output Tipor_I,
  output Tipor_S,
  output Tipor_B,
  output Tipor_J
);

  and and_1 (Tipor_R, Opcode[0], Opcode[1], ~Opcode[2], ~Opcode[3], Opcode[4], Opcode[5], ~Opcode[6]);  // AND_Gate
  and and_2 (Tipor_I, Opcode[0], Opcode[1], ~Opcode[2], ~Opcode[3], ~Opcode[5], ~Opcode[6]);  // AND_Gate
  and and_3 (Tipor_S, Opcode[0], Opcode[1], ~Opcode[2], ~Opcode[3], ~Opcode[4], Opcode[5], ~Opcode[6]);  // AND_Gate
  and and_4 (Tipor_B, Opcode[0], Opcode[1], ~Opcode[2], ~Opcode[3], ~Opcode[4], Opcode[5], Opcode[6]);  // AND_Gate
  and and_5 (Tipor_J, Opcode[0], Opcode[1], Opcode[2], Opcode[3], ~Opcode[4], Opcode[5], Opcode[6]);  // AND_Gate
endmodule
