// Logisim project immediate_generator.circ as structural Verilog: 1 circuit, main circuit main
module main (
  input  [1:0] ImmSrc,
  input  [31:0] in_2,
  output [31:0] out_3
);

  wire [31:0] bit_extender_1_out, bit_extender_2_out, bit_extender_3_out, bit_extender_4_out;

  assign bit_extender_1_out = {{20{in_2[31]}}, in_2[31:20]};  // Bit_Extender bit_extender_1
  assign bit_extender_2_out = {{20{in_2[31]}}, {in_2[31:25], in_2[11:7]}};  // Bit_Extender bit_extender_2
  assign bit_extender_3_out = {{19{in_2[31]}}, {in_2[31:30], in_2[7], in_2[29:25], in_2[11:8], 1'b0}};  // Bit_Extender bit_extender_3
  assign bit_extender_4_out = {{11{in_2[31]}}, {in_2[31], in_2[19:12], in_2[20], in_2[30:21], 1'b0}};  // Bit_Extender bit_extender_4
  Multiplexer #(.select(2), .width(32), .enable("false")) multiplexer_1 (
    .in0(bit_extender_1_out), .in1(bit_extender_2_out), .in2(bit_extender_3_out), .in3(bit_extender_4_out),
    .out(out_3), .sel(ImmSrc));
endmodule
