// Logisim project monociclo.circ as structural Verilog: 1 circuit, main circuit main
module main (
);

  wire and_1_out, dipswitch_1_p1, main_2_alusrc, main_2_branch, main_2_jalornot, main_2_memtoreg,
       main_2_regwrite, main_5_zero, main_6_uc_ula, MemWrite, or_1_out;
  wire [1:0] main_2_alucontrol, main_2_immsrc;
  wire [23:0] main_1_out_2, main_7_out_2;
  wire [31:0] adder_1_out, adder_2_out, main_3_out_3, main_4_rs1_2, main_4_rs2_2, main_5_aluoutput,
       \Memória_de_Dados_data , \Memória_de_Instrução_data , multiplexer_1_out, multiplexer_2_out,
       multiplexer_3_out, multiplexer_4_out, PC_q;

  Multiplexer #(.width(32), .enable("false")) multiplexer_1 (
    .in0(adder_1_out), .in1(adder_2_out), .out(multiplexer_1_out), .sel(or_1_out));
  // DipSwitch #(.NSwitches(1)) dipswitch_1: pin names not known; wires that end beside it: dipswitch_1_p1
  Register #(.width(32), .Select("low")) PC (.D(multiplexer_1_out), .Q(PC_q), .clk(dipswitch_1_p1));  // open: en, clr
  Adder #(.width(32)) adder_1 (.a(PC_q), .b(32'h4), .out(adder_1_out));  // open: cin, cout
  conversor_32_para_24_main main_1 (.Entrada(PC_q), .out_2(main_1_out_2));
  RAM #(.addrWidth(24), .dataWidth(32), .bus("asynch"), .Select("low")) \Memória_de_Instrução  (
    .addr(main_1_out_2), .data(\Memória_de_Instrução_data ), .ld(1'b1));  // open: sel, clr
  unidade_controle_main main_2 (
    .ImmSrc(main_2_immsrc), .ALUSrc(main_2_alusrc), .ALUControl(main_2_alucontrol), .MemWrite(MemWrite),
    .MemToReg(main_2_memtoreg), .JalOrNot(main_2_jalornot), .RegWrite(main_2_regwrite),
    .Branch(main_2_branch), .Opcode(\Memória_de_Instrução_data [6:0]));
  immediate_generator_main main_3 (.out_3(main_3_out_3), .in_2(\Memória_de_Instrução_data ), .ImmSrc(main_2_immsrc));
  banco_de_resgitradores_main main_4 (
    .Clock(dipswitch_1_p1), .WriteData(multiplexer_2_out), .rd(\Memória_de_Instrução_data [11:7]),
    .rs1(\Memória_de_Instrução_data [24:20]), .rs2(\Memória_de_Instrução_data [19:15]),
    .RegWrite(main_2_regwrite), .rs2_2(main_4_rs2_2), .rs1_2(main_4_rs1_2));
  Multiplexer #(.width(32), .enable("false")) multiplexer_2 (
    .in0(multiplexer_4_out), .in1(adder_1_out), .out(multiplexer_2_out), .sel(main_2_jalornot));
  Multiplexer #(.width(32), .enable("false")) multiplexer_3 (
    .in0(main_4_rs2_2), .in1(main_3_out_3), .out(multiplexer_3_out), .sel(main_2_alusrc));
  Adder #(.width(32)) adder_2 (.a(main_3_out_3), .b(PC_q), .out(adder_2_out));  // open: cin, cout
  or or_1 (or_1_out, main_2_jalornot, and_1_out);
  and and_1 (and_1_out, main_2_branch, main_5_zero);
  unidade_logica_aritmetica_main main_5 (
    .ALUOutput(main_5_aluoutput), .B(multiplexer_3_out), .A(main_4_rs1_2), .ALUControl(main_6_uc_ula),
    .Zero(main_5_zero));
  unidade_controle_ula_main main_6 (
    .ALUControl(main_2_alucontrol), .f3(\Memória_de_Instrução_data [14:12]),
    .f7(\Memória_de_Instrução_data [31:25]), .UC_ULA(main_6_uc_ula));
  conversor_32_para_24_main main_7 (.Entrada(main_5_aluoutput), .out_2(main_7_out_2));
  RAM #(.addrWidth(24), .dataWidth(32), .bus("separate"), .simpleMode("false"), .Select("low")) \Memória_de_Dados  (
    .addr(main_7_out_2), .din(main_4_rs2_2), .data(\Memória_de_Dados_data ), .str(MemWrite),
    .clk(dipswitch_1_p1));  // open: sel, ld, clr
  Multiplexer #(.width(32), .enable("false")) multiplexer_4 (
    .in0(main_5_aluoutput), .in1(\Memória_de_Dados_data ), .out(multiplexer_4_out), .sel(main_2_memtoreg));

  // Notes on the sheet:
  //   para manter a realidade
  //   Cada endereço da RAM armazena 4 bytes, logo para avançar,
  //   em teoria, deveria somar 1 para PC, mas vamos manter PC + 4
endmodule
