// Logisim project pipeline.circ as structural Verilog: 1 circuit, main circuit main
module main (
);

  wire and_1_out, dipswitch_1_p1, EX_MEM_Branch_q, EX_MEM_JalOrNot_q, EX_MEM_MemToReg_q, EX_MEM_RegWrite_q,
       EX_MEM_Zero_q, ID_EX_ALUSrc_q, ID_EX_Branch_q, ID_EX_JalOrNot_q, ID_EX_MemToReg_q, ID_EX_MemWrite_q,
       ID_EX_RegWrite_q, main_2_alusrc, main_2_branch, main_2_jalornot, main_2_memtoreg, main_2_memwrite,
       main_2_regwrite, main_5_zero, main_6_uc_ula, MEM_WB_Branch_q, MEM_WB_JalOrNot_q, MEM_WB_MemToReg_q,
       MEM_WB_RegWrite_q, MEM_WB_Zero_q, MemWrite, not_1_out, or_1_out;
  wire [1:0] ID_EX_ALUControl_q, main_2_alucontrol, main_2_immsrc;
  wire [2:0] ID_EX_f3_q;
  wire [4:0] EX_MEM_rd_q, ID_EX_rd_q, MEM_WB_rd_q;
  wire [6:0] ID_EX_f7_q;
  wire [23:0] main_1_out_2, main_7_out_2;
  wire [31:0] adder_1_out, adder_2_out, EX_MEM_ALUOutput_q, EX_MEM_B_q, EX_MEM_PC_4_q, EX_MEM_PC_Imm_q,
       ID_EX_A_q, ID_EX_B_q, ID_EX_Imm_q, ID_EX_PC_4_q, ID_EX_PC_q, IF_ID_IR_q, IF_ID_PC___4_q, IF_ID_PC_q,
       main_3_rs1_2, main_3_rs2_2, main_4_out_3, main_5_aluoutput, MEM_WB_ALUOutput_q, MEM_WB_LMD_q,
       MEM_WB_PC_4_q, MEM_WB_PC_Imm_q, \Memória_de_Dados_data , \Memória_de_Instrução_data ,
       multiplexer_1_out, multiplexer_2_out, multiplexer_3_out, multiplexer_4_out, PC_q;

  // DipSwitch #(.NSwitches(1)) dipswitch_1: pin names not known; wires that end beside it: dipswitch_1_p1
  Register #(.width(32), .Select("low")) PC (.D(multiplexer_1_out), .Q(PC_q), .clk(dipswitch_1_p1));  // open: en, clr
  Multiplexer #(.width(32), .enable("false")) multiplexer_1 (
    .in0(adder_1_out), .in1(MEM_WB_PC_Imm_q), .out(multiplexer_1_out), .sel(or_1_out));
  Adder #(.width(32)) adder_1 (.a(PC_q), .b(32'h4), .out(adder_1_out));  // open: cin, cout
  conversor_32_para_24_main main_1 (.Entrada(PC_q), .out_2(main_1_out_2));
  RAM #(.addrWidth(24), .dataWidth(32), .bus("asynch"), .Select("low")) \Memória_de_Instrução  (
    .addr(main_1_out_2), .data(\Memória_de_Instrução_data ), .ld(1'b1));  // open: sel, clr
  Register #(.width(32), .Select("low")) IF_ID_IR (
    .D(\Memória_de_Instrução_data ), .Q(IF_ID_IR_q), .clk(dipswitch_1_p1));  // open: en, clr
  Register #(.width(32), .Select("low")) IF_ID_PC___4 (
    .D(adder_1_out), .Q(IF_ID_PC___4_q), .clk(dipswitch_1_p1));  // open: en, clr
  Register #(.width(32), .Select("low")) IF_ID_PC (.D(PC_q), .Q(IF_ID_PC_q), .clk(dipswitch_1_p1));  // open: en, clr
  unidade_controle_main main_2 (
    .ImmSrc(main_2_immsrc), .ALUSrc(main_2_alusrc), .ALUControl(main_2_alucontrol),
    .MemWrite(main_2_memwrite), .MemToReg(main_2_memtoreg), .JalOrNot(main_2_jalornot),
    .RegWrite(main_2_regwrite), .Branch(main_2_branch), .Opcode(IF_ID_IR_q[6:0]));
  banco_de_resgitradores_main main_3 (
    .Clock(not_1_out), .WriteData(multiplexer_4_out), .rd(MEM_WB_rd_q), .rs1(IF_ID_IR_q[24:20]),
    .rs2(IF_ID_IR_q[19:15]), .RegWrite(MEM_WB_RegWrite_q), .rs2_2(main_3_rs2_2), .rs1_2(main_3_rs1_2));
  immediate_generator_main main_4 (.out_3(main_4_out_3), .in_2(IF_ID_IR_q), .ImmSrc(main_2_immsrc));
  not not_1 (not_1_out, dipswitch_1_p1);
  Register #(.width(1), .Select("low")) ID_EX_ALUSrc (
    .D(main_2_alusrc), .Q(ID_EX_ALUSrc_q), .clk(dipswitch_1_p1));  // open: en, clr
  Register #(.width(2), .Select("low")) ID_EX_ALUControl (
    .D(main_2_alucontrol), .Q(ID_EX_ALUControl_q), .clk(dipswitch_1_p1));  // open: en, clr
  Register #(.width(1), .Select("low")) ID_EX_MemWrite (
    .D(main_2_memwrite), .Q(ID_EX_MemWrite_q), .clk(dipswitch_1_p1));  // open: en, clr
  Register #(.width(1), .Select("low")) ID_EX_MemToReg (
    .D(main_2_memtoreg), .Q(ID_EX_MemToReg_q), .clk(dipswitch_1_p1));  // open: en, clr
  Register #(.width(1), .Select("low")) ID_EX_JalOrNot (
    .D(main_2_jalornot), .Q(ID_EX_JalOrNot_q), .clk(dipswitch_1_p1));  // open: en, clr
  Register #(.width(1), .Select("low")) ID_EX_RegWrite (
    .D(main_2_regwrite), .Q(ID_EX_RegWrite_q), .clk(dipswitch_1_p1));  // open: en, clr
  Register #(.width(1), .Select("low")) ID_EX_Branch (
    .D(main_2_branch), .Q(ID_EX_Branch_q), .clk(dipswitch_1_p1));  // open: en, clr
  Register #(.width(32), .Select("low")) ID_EX_A (
    .D(main_3_rs1_2), .Q(ID_EX_A_q), .clk(dipswitch_1_p1));  // open: en, clr
  Register #(.width(32), .Select("low")) ID_EX_B (
    .D(main_3_rs2_2), .Q(ID_EX_B_q), .clk(dipswitch_1_p1));  // open: en, clr
  Register #(.width(5), .Select("low")) ID_EX_rd (
    .D(IF_ID_IR_q[11:7]), .Q(ID_EX_rd_q), .clk(dipswitch_1_p1));  // open: en, clr
  Register #(.width(32), .Select("low")) ID_EX_PC_4 (
    .D(IF_ID_PC___4_q), .Q(ID_EX_PC_4_q), .clk(dipswitch_1_p1));  // open: en, clr
  Register #(.width(3), .Select("low")) ID_EX_f3 (
    .D(IF_ID_IR_q[14:12]), .Q(ID_EX_f3_q), .clk(dipswitch_1_p1));  // open: en, clr
  Register #(.width(7), .Select("low")) ID_EX_f7 (
    .D(IF_ID_IR_q[31:25]), .Q(ID_EX_f7_q), .clk(dipswitch_1_p1));  // open: en, clr
  Register #(.width(32), .Select("low")) ID_EX_Imm (
    .D(main_4_out_3), .Q(ID_EX_Imm_q), .clk(dipswitch_1_p1));  // open: en, clr
  Register #(.width(32), .Select("low")) ID_EX_PC (
    .D(IF_ID_PC_q), .Q(ID_EX_PC_q), .clk(dipswitch_1_p1));  // open: en, clr
  unidade_logica_aritmetica_main main_5 (
    .ALUOutput(main_5_aluoutput), .B(multiplexer_2_out), .A(ID_EX_A_q), .ALUControl(main_6_uc_ula),
    .Zero(main_5_zero));
  Multiplexer #(.width(32), .enable("false")) multiplexer_2 (
    .in0(ID_EX_B_q), .in1(ID_EX_Imm_q), .out(multiplexer_2_out), .sel(ID_EX_ALUSrc_q));
  unidade_controle_ula_main main_6 (
    .ALUControl(ID_EX_ALUControl_q), .f3(ID_EX_f3_q), .f7(ID_EX_f7_q), .UC_ULA(main_6_uc_ula));
  Adder #(.width(32)) adder_2 (.a(ID_EX_Imm_q), .b(ID_EX_PC_q), .out(adder_2_out));  // open: cin, cout
  Register #(.width(1), .Select("low")) EX_MEM_Zero (
    .D(main_5_zero), .Q(EX_MEM_Zero_q), .clk(dipswitch_1_p1));  // open: en, clr
  Register #(.width(1), .Select("low")) EX_MEM_MemWrite (
    .D(ID_EX_MemWrite_q), .Q(MemWrite), .clk(dipswitch_1_p1));  // open: en, clr
  Register #(.width(1), .Select("low")) EX_MEM_MemToReg (
    .D(ID_EX_MemToReg_q), .Q(EX_MEM_MemToReg_q), .clk(dipswitch_1_p1));  // open: en, clr
  Register #(.width(1), .Select("low")) EX_MEM_JalOrNot (
    .D(ID_EX_JalOrNot_q), .Q(EX_MEM_JalOrNot_q), .clk(dipswitch_1_p1));  // open: en, clr
  Register #(.width(1), .Select("low")) EX_MEM_RegWrite (
    .D(ID_EX_RegWrite_q), .Q(EX_MEM_RegWrite_q), .clk(dipswitch_1_p1));  // open: en, clr
  Register #(.width(1), .Select("low")) EX_MEM_Branch (
    .D(ID_EX_Branch_q), .Q(EX_MEM_Branch_q), .clk(dipswitch_1_p1));  // open: en, clr
  Register #(.width(32), .Select("low")) EX_MEM_ALUOutput (
    .D(main_5_aluoutput), .Q(EX_MEM_ALUOutput_q), .clk(dipswitch_1_p1));  // open: en, clr
  Register #(.width(32), .Select("low")) EX_MEM_B (
    .D(ID_EX_B_q), .Q(EX_MEM_B_q), .clk(dipswitch_1_p1));  // open: en, clr
  Register #(.width(5), .Select("low")) EX_MEM_rd (
    .D(ID_EX_rd_q), .Q(EX_MEM_rd_q), .clk(dipswitch_1_p1));  // open: en, clr
  Register #(.width(32), .Select("low")) EX_MEM_PC_4 (
    .D(ID_EX_PC_4_q), .Q(EX_MEM_PC_4_q), .clk(dipswitch_1_p1));  // open: en, clr
  Register #(.width(32), .Select("low")) EX_MEM_PC_Imm (
    .D(adder_2_out), .Q(EX_MEM_PC_Imm_q), .clk(dipswitch_1_p1));  // open: en, clr
  conversor_32_para_24_main main_7 (.Entrada(EX_MEM_ALUOutput_q), .out_2(main_7_out_2));
  RAM #(.addrWidth(24), .dataWidth(32), .bus("separate"), .simpleMode("false"), .Select("low")) \Memória_de_Dados  (
    .addr(main_7_out_2), .din(EX_MEM_B_q), .data(\Memória_de_Dados_data ), .str(MemWrite),
    .clk(dipswitch_1_p1));  // open: sel, ld, clr
  Register #(.width(1), .Select("low")) MEM_WB_Zero (
    .D(EX_MEM_Zero_q), .Q(MEM_WB_Zero_q), .clk(dipswitch_1_p1));  // open: en, clr
  Register #(.width(1), .Select("low")) MEM_WB_MemToReg (
    .D(EX_MEM_MemToReg_q), .Q(MEM_WB_MemToReg_q), .clk(dipswitch_1_p1));  // open: en, clr
  Register #(.width(1), .Select("low")) MEM_WB_JalOrNot (
    .D(EX_MEM_JalOrNot_q), .Q(MEM_WB_JalOrNot_q), .clk(dipswitch_1_p1));  // open: en, clr
  Register #(.width(1), .Select("low")) MEM_WB_RegWrite (
    .D(EX_MEM_RegWrite_q), .Q(MEM_WB_RegWrite_q), .clk(dipswitch_1_p1));  // open: en, clr
  Register #(.width(1), .Select("low")) MEM_WB_Branch (
    .D(EX_MEM_Branch_q), .Q(MEM_WB_Branch_q), .clk(dipswitch_1_p1));  // open: en, clr
  Register #(.width(32), .Select("low")) MEM_WB_ALUOutput (
    .D(EX_MEM_ALUOutput_q), .Q(MEM_WB_ALUOutput_q), .clk(dipswitch_1_p1));  // open: en, clr
  Register #(.width(32), .Select("low")) MEM_WB_LMD (
    .D(\Memória_de_Dados_data ), .Q(MEM_WB_LMD_q), .clk(dipswitch_1_p1));  // open: en, clr
  Register #(.width(5), .Select("low")) MEM_WB_rd (
    .D(EX_MEM_rd_q), .Q(MEM_WB_rd_q), .clk(dipswitch_1_p1));  // open: en, clr
  Register #(.width(32), .Select("low")) MEM_WB_PC_4 (
    .D(EX_MEM_PC_4_q), .Q(MEM_WB_PC_4_q), .clk(dipswitch_1_p1));  // open: en, clr
  Register #(.width(32), .Select("low")) MEM_WB_PC_Imm (
    .D(EX_MEM_PC_Imm_q), .Q(MEM_WB_PC_Imm_q), .clk(dipswitch_1_p1));  // open: en, clr
  or or_1 (or_1_out, and_1_out, MEM_WB_JalOrNot_q);
  and and_1 (and_1_out, MEM_WB_Zero_q, MEM_WB_Branch_q);
  Multiplexer #(.width(32), .enable("false")) multiplexer_3 (
    .in0(MEM_WB_ALUOutput_q), .in1(MEM_WB_LMD_q), .out(multiplexer_3_out), .sel(MEM_WB_MemToReg_q));
  Multiplexer #(.width(32), .enable("false")) multiplexer_4 (
    .in0(multiplexer_3_out), .in1(MEM_WB_PC_4_q), .out(multiplexer_4_out), .sel(MEM_WB_JalOrNot_q));

  // Notes on the sheet:
  //   para manter a realidade
  //   Cada endereço da RAM armazena 4 bytes, logo para avançar,
  //   em teoria, deveria somar 1 para PC, mas vamos manter PC + 4
endmodule
