// Logisim project unidade_controle.circ as structural Verilog: 1 circuit, main circuit main
module main (
  input  [6:0] Opcode,
  output [1:0] ImmSrc,
  output ALUSrc,
  output [1:0] ALUControl,
  output MemWrite,
  output MemToReg,
  output JalOrNot,
  output RegWrite,
  output Branch
);

  detector_tipo_instrucao_main main_1 (
    .Opcode(Opcode), .Tipor_R(ALUControl[1]), .Tipor_I(MemToReg), .Tipor_S(MemWrite),
    .Tipor_B(ALUControl[0]), .Tipor_J(JalOrNot));
  or or_1 (ImmSrc[0], MemWrite, JalOrNot);
  or or_2 (ImmSrc[1], ALUControl[0], JalOrNot);
  or or_3 (ALUSrc, MemToReg, MemWrite);
  or or_4 (RegWrite, ALUControl[1], MemToReg, JalOrNot);

  assign Branch = ALUControl[0];
endmodule
