// Logisim project unidade_controle_ula.circ as structural Verilog: 1 circuit, main circuit main
module main (
  input  [1:0] ALUControl,
  input  [2:0] f3,
  input  [6:0] f7,
  output UC_ULA
);


  assign UC_ULA = ALUControl[0];
endmodule
