// Logisim project unidade_logica_aritmetica.circ as structural Verilog: 1 circuit, main circuit main
module main (
  input  ALUControl,
  input  [31:0] B,
  input  [31:0] A,
  output [31:0] ALUOutput,
  output Zero
);

  wire [31:0] adder_1_out, subtractor_1_out;

  Adder #(.width(32)) adder_1 (.a(A), .b(B), .out(adder_1_out));  // open: cin, cout
  Subtractor #(.width(32)) subtractor_1 (.a(A), .b(B), .out(subtractor_1_out));  // open: bin, bout
  Multiplexer #(.width(32), .enable("false")) multiplexer_1 (
    .in0(adder_1_out), .in1(subtractor_1_out), .out(ALUOutput), .sel(ALUControl));
  nor nor_1 (Zero, ALUOutput[0], ALUOutput[1], ALUOutput[2], ALUOutput[3], ALUOutput[4], ALUOutput[5], ALUOutput[6], ALUOutput[7], ALUOutput[8], ALUOutput[9], ALUOutput[10], ALUOutput[11], ALUOutput[12], ALUOutput[13], ALUOutput[14], ALUOutput[15], ALUOutput[17], ALUOutput[18], ALUOutput[19], ALUOutput[20], ALUOutput[21], ALUOutput[22], ALUOutput[23], ALUOutput[24], ALUOutput[25], ALUOutput[26], ALUOutput[27], ALUOutput[28], ALUOutput[29], ALUOutput[30], ALUOutput[31], ALUOutput[16]);
endmodule
